// Logisim project bots.circ as structural Verilog: 1 circuit, main circuit main
module main (
  input  CURR_PLAYER,
  input  PREP_PHASE_END,
  input  CLR,
  input  CLK,
  input  [3:0] SHIPS_NUMBER,
  output ROTATED,
  output CONFIRM,
  output [3:0] X,
  output [3:0] Y
);

  wire _1X1_SHIP, _1X2_SHIP, _1X3_SHIP, _1X4_SHIP, _10SHIPS, and_2_out, BOOT_PHASE, CLK_t, comparator_1_eq,
       comparator_1_gt, comparator_3_lt, comparator_4_gt, comparator_4_lt, demultiplexer_1_out0,
       demultiplexer_1_out1, demultiplexer_1_out2, not_1_out, not_2_out, not_3_out, not_4_out,
       POSITION_CLOCK, random_1_out, random_2_out, random_3_out, random_4_out, random_5_out, random_6_out,
       ROTATION_CLOCK, SHOOT_ONCE_PHASE;
  wire [3:0] undriven;
  wire [4:0] counter_1_q;

  Clock clock_1 (.out(CLK_t));
  Comparator #(.width(4), .mode("unsigned")) comparator_1 (
    .a(SHIPS_NUMBER), .b(4'b1010), .gt(comparator_1_gt), .eq(comparator_1_eq));  // open: lt
  and and_1 (SHOOT_ONCE_PHASE, CURR_PLAYER, PREP_PHASE_END);
  not not_1 (not_1_out, PREP_PHASE_END);
  not not_2 (not_2_out, _10SHIPS);
  or or_1 (_10SHIPS, comparator_1_gt, comparator_1_eq);
  and and_2 (and_2_out, BOOT_PHASE, CLK_t);
  and and_3 (BOOT_PHASE, not_1_out, not_2_out);
  Demultiplexer #(.select(5)) demultiplexer_1 (
    .out0(demultiplexer_1_out0), .out1(demultiplexer_1_out1), .out2(demultiplexer_1_out2), .in(1'b1),
    .sel(counter_1_q));  // open: out3, out4, out5, out6, out7, out8, out9, out10, out11, out12, out13, out14, out15, out16, out17, out18, out19, out20, out21, out22, out23, out24, out25, out26, out27, out28, out29, out30, out31, en
  Counter #(.width(5), .max('h1f)) counter_1 (
    .Q(counter_1_q), .clk(and_2_out), .clr(CLR));  // open: load, D, count, carry
  Comparator #(.width(4)) comparator_2 (.a(SHIPS_NUMBER), .b(4'b0100), .lt(_1X1_SHIP));  // open: gt, eq
  not not_3 (not_3_out, _1X1_SHIP);
  Comparator #(.width(4)) comparator_3 (.a(SHIPS_NUMBER), .b(4'b0111), .lt(comparator_3_lt));  // open: gt, eq
  Comparator #(.width(4)) comparator_4 (
    .a(undriven), .b(4'b1001), .gt(comparator_4_gt), .eq(_1X4_SHIP), .lt(comparator_4_lt));
  // Probe on 4'b1001
  and and_4 (_1X2_SHIP, not_3_out, comparator_3_lt);
  not not_4 (not_4_out, _1X2_SHIP);
  and and_5 (_1X3_SHIP, not_4_out, comparator_4_lt);
  assign ROTATION_CLOCK = and_2_out ? demultiplexer_1_out0 : 1'bz;  // Controlled_Buffer controlled_buffer_1
  assign POSITION_CLOCK = and_2_out ? demultiplexer_1_out1 : 1'bz;  // Controlled_Buffer controlled_buffer_2
  assign CONFIRM = and_2_out ? demultiplexer_1_out2 : 1'bz;  // Controlled_Buffer controlled_buffer_3
  Random #(.width(1)) random_1 (.out(random_1_out));  // open: clk, next, clr
  Random #(.width(1)) random_2 (.out(random_2_out));  // open: clk, next, clr
  Random #(.width(1)) random_3 (.out(random_3_out));  // open: clk, next, clr
  Random #(.width(1)) random_4 (.out(random_4_out));  // open: clk, next, clr
  Random #(.width(1)) random_5 (.out(random_5_out));  // open: clk, next, clr
  Random #(.width(1)) random_6 (.clk(ROTATION_CLOCK), .next(ROTATION_CLOCK), .out(random_6_out));  // open: clr
  Counter #(.width(1), .max('h1)) counter_2 (
    .Q(ROTATED), .clk(random_6_out), .clr(CLR));  // open: load, D, count, carry
  random_num_generator_A_main main_1 (.GENERATE(POSITION_CLOCK), .OUTPUT(X));
  random_num_generator_B_main main_2 (.GENERATE(POSITION_CLOCK), .OUTPUT(Y));

  // Other names for the same wires on the sheet: CONFIRM_CLOCK = CONFIRM; SHIP_NUMBER[3:0] = SHIPS_NUMBER
endmodule
