// Logisim project memory_management.circ as structural Verilog: 1 circuit, main circuit main
module main (
  input  [3:0] X,
  input  [3:0] Y,
  input  ROTATED,
  input  [3:0] CHECK_X,
  input  [3:0] CHECK_Y,
  output [14:0] RAM_OUT,
  output out_7,
  output out_8
);

  wire and_1_out, and_2_out, and_3_out, and_4_out, and_5_out, and_6_out, and_7_out, and_8_out, and_9_out,
       and_10_out, and_11_out, CHECK, CHECK_OCCUPIED_RST, CHECKING, CLEAR_2_out, CLEAR_out, CLK_2_out,
       CLK_out, comparator_1_eq, comparator_2_eq, comparator_3_eq, comparator_4_eq, comparator_5_eq,
       comparator_6_eq, comparator_7_eq, comparator_8_eq, comparator_9_eq, comparator_10_eq, CONFIRM,
       main_1_p3, main_2_p4, main_4_p6, main_4_p7, not_1_out, not_2_out, or_1_out, or_2_out;
  wire [3:0] adder_1_out, adder_2_out, adder_3_out, adder_4_out, adder_5_out, adder_6_out, CURR_SHIP_CHECK,
       CURRENT_SHIP, MEM_SELECT;
  wire [7:0] HORI_CHECK, VERT_CHECK;
  wire [14:8] SHIP_DATA;

  Button u_CONFIRM (.out(CONFIRM));
  Multiplexer #(.select(2), .width(4), .enable("false")) multiplexer_1 (
    .in0(4'b0001), .in1(4'b0011), .in2(4'b0111), .in3(4'b1111), .out(SHIP_DATA[14:11]), .sel(SHIP_DATA[9:8]));
  assign RAM_OUT = CONFIRM ? {SHIP_DATA[14:11], ROTATED, SHIP_DATA[9:8], Y, X} : 15'bz;  // Controlled_Buffer controlled_buffer_1
  Button u_CHECK (.out(CHECK));
  Demultiplexer #(.width(8), .enable("false")) demultiplexer_1 (
    .out0(VERT_CHECK), .out1(HORI_CHECK), .in(RAM_OUT[7:0]), .sel(RAM_OUT[10]));
  not not_1 (not_1_out, CONFIRM);
  Clock CLK (.out(CLK_out));
  RAM #(.addrWidth(4), .dataWidth(15)) ram_1 (
    .addr(MEM_SELECT), .data(RAM_OUT), .clk(CLK_out), .ld(not_1_out));  // open: sel, clr
  D_Flip_Flop d_ff_1 (.clk(CHECK), .D(CHECK), .Q(CHECKING), .reset(CHECK_OCCUPIED_RST));  // open: Qn, preset, en
  Counter #(.width(4), .max('h9), .trigger("falling")) counter_1 (
    .Q(CURRENT_SHIP), .clk(CONFIRM));  // open: load, D, count, carry, clr
  Counter #(.width(4), .max('h9), .trigger("falling")) counter_2 (
    .Q(CURR_SHIP_CHECK), .carry(CHECK_OCCUPIED_RST), .clk(and_1_out), .clr(CHECK_OCCUPIED_RST));  // open: load, D, count
  and and_1 (and_1_out, CLK_2_out, CHECKING);
  Clock CLK_2 (.out(CLK_2_out));
  // Probe on MEM_SELECT
  assign MEM_SELECT = not_2_out ? CURRENT_SHIP : 4'bz;  // Controlled_Buffer controlled_buffer_2
  not not_2 (not_2_out, CHECKING);
  assign MEM_SELECT = CHECKING ? CURR_SHIP_CHECK : 4'bz;  // Controlled_Buffer controlled_buffer_3
  Comparator #(.width(4)) comparator_1 (.a(CHECK_X), .b(VERT_CHECK[3:0]), .eq(comparator_1_eq));  // open: gt, lt
  Adder #(.width(4)) adder_1 (.a(VERT_CHECK[7:4]), .b(4'b0001), .out(adder_1_out));  // open: cin, cout
  Adder #(.width(4)) adder_2 (.a(VERT_CHECK[7:4]), .b(4'b0010), .out(adder_2_out));  // open: cin, cout
  Adder #(.width(4)) adder_3 (.a(VERT_CHECK[7:4]), .b(4'b0011), .out(adder_3_out));  // open: cin, cout
  Comparator #(.width(4)) comparator_2 (.a(CHECK_Y), .b(HORI_CHECK[7:4]), .eq(comparator_2_eq));  // open: gt, lt
  Adder #(.width(4)) adder_4 (.a(HORI_CHECK[3:0]), .b(4'b0001), .out(adder_4_out));  // open: cin, cout
  Adder #(.width(4)) adder_5 (.a(HORI_CHECK[3:0]), .b(4'b0010), .out(adder_5_out));  // open: cin, cout
  Adder #(.width(4)) adder_6 (.a(HORI_CHECK[3:0]), .b(4'b0011), .out(adder_6_out));  // open: cin, cout
  Comparator #(.width(4), .mode("unsigned")) comparator_3 (
    .a(CHECK_Y), .b(VERT_CHECK[7:4]), .eq(comparator_3_eq));  // open: gt, lt
  Comparator #(.width(4), .mode("unsigned")) comparator_4 (
    .a(CHECK_Y), .b(adder_1_out), .eq(comparator_4_eq));  // open: gt, lt
  Comparator #(.width(4), .mode("unsigned")) comparator_5 (
    .a(CHECK_Y), .b(adder_2_out), .eq(comparator_5_eq));  // open: gt, lt
  Comparator #(.width(4), .mode("unsigned")) comparator_6 (
    .a(CHECK_Y), .b(adder_3_out), .eq(comparator_6_eq));  // open: gt, lt
  Comparator #(.width(4), .mode("unsigned")) comparator_7 (
    .a(CHECK_X), .b(HORI_CHECK[3:0]), .eq(comparator_7_eq));  // open: gt, lt
  Comparator #(.width(4), .mode("unsigned")) comparator_8 (
    .a(CHECK_X), .b(adder_4_out), .eq(comparator_8_eq));  // open: gt, lt
  Comparator #(.width(4), .mode("unsigned")) comparator_9 (
    .a(CHECK_X), .b(adder_5_out), .eq(comparator_9_eq));  // open: gt, lt
  Comparator #(.width(4), .mode("unsigned")) comparator_10 (
    .a(CHECK_X), .b(adder_6_out), .eq(comparator_10_eq));  // open: gt, lt
  // _4bit_greater_or_equal_than_and_less_than_main main_1: pin names not known; wires that end beside it: CURRENT_SHIP, 4'b0000, main_1_p3
  // _4bit_greater_or_equal_than_and_less_than_main main_2: pin names not known; wires that end beside it: 4'b0100, CURRENT_SHIP, 4'b0100, main_2_p4
  // _4bit_greater_or_equal_than_and_less_than_main main_3: pin names not known; wires that end beside it: 4'b0111, CURRENT_SHIP
  // _4bit_greater_or_equal_than_and_less_than_main main_4: pin names not known; wires that end beside it: 4'b0111, 4'b1001, CURRENT_SHIP, 4'b1001, 4'b1010, main_4_p6, main_4_p7
  and and_2 (and_2_out, comparator_3_eq, RAM_OUT[11]);
  and and_3 (and_3_out, comparator_4_eq, RAM_OUT[12]);
  and and_4 (and_4_out, comparator_5_eq, RAM_OUT[13]);
  and and_5 (and_5_out, comparator_6_eq, RAM_OUT[14]);
  and and_6 (and_6_out, comparator_7_eq, RAM_OUT[11]);
  and and_7 (and_7_out, comparator_8_eq, RAM_OUT[12]);
  and and_8 (and_8_out, comparator_9_eq, RAM_OUT[13]);
  and and_9 (and_9_out, comparator_10_eq, RAM_OUT[14]);
  assign SHIP_DATA[9:8] = main_1_p3 ? 2'b00 : 2'bz;  // Controlled_Buffer controlled_buffer_4
  Pull_Resistor pull_resistor_1 (.node(SHIP_DATA[9:8]));
  assign SHIP_DATA[9:8] = main_2_p4 ? 2'b01 : 2'bz;  // Controlled_Buffer controlled_buffer_5
  Pull_Resistor pull_resistor_2 (.node(SHIP_DATA[9:8]));
  Pull_Resistor pull_resistor_3 (.node(SHIP_DATA[9:8]));
  assign SHIP_DATA[9:8] = main_4_p6 ? 2'b10 : 2'bz;  // Controlled_Buffer controlled_buffer_6
  assign SHIP_DATA[9:8] = main_4_p7 ? 2'b11 : 2'bz;  // Controlled_Buffer controlled_buffer_7
  Pull_Resistor pull_resistor_4 (.node(SHIP_DATA[9:8]));
  or or_1 (or_1_out, and_2_out, and_3_out, and_4_out, and_5_out);
  or or_2 (or_2_out, and_6_out, and_7_out, and_8_out, and_9_out);
  and and_10 (and_10_out, CHECKING, ~RAM_OUT[10], comparator_1_eq, or_1_out);  // AND_Gate
  D_Flip_Flop d_ff_2 (.clk(and_10_out), .D(and_10_out), .Q(out_7), .reset(CLEAR_out));  // open: Qn, preset, en
  Button CLEAR (.out(CLEAR_out));
  D_Flip_Flop d_ff_3 (.clk(and_11_out), .D(and_11_out), .Q(out_8), .reset(CLEAR_2_out));  // open: Qn, preset, en
  and and_11 (and_11_out, CHECKING, RAM_OUT[10], comparator_2_eq, or_2_out);
  Button CLEAR_2 (.out(CLEAR_2_out));

  // Other names for the same wires on the sheet: ROTATED_CHECK = RAM_OUT[10]; ALIVE0 = RAM_OUT[11];
  //   ALIVE1 = RAM_OUT[12]; ALIVE2 = RAM_OUT[13]; ALIVE3 = RAM_OUT[14]; SHIP_DATA (some bits) = {ROTATED, Y, X};
  //   SHIP_X[3:0] = X; SHIP_Y[3:0] = Y; SHIP_TYPE[1:0] = SHIP_DATA[9:8]; IS_ROTATED = ROTATED
endmodule
